# Fritzing sketch weatherStation1 (saved by Fritzing 0.9.3b)
breadboards: 2
perfboards: 1

parts:
  M1 = DOIT Esp32 DevKit v1 (30 pins long, 11 pins width) [part_number=ESP32S-PIN30]
  7V = SOLAR-IXYS [package=solarbit-12x1]
  DS1 = DS18B20 1-Wire Temperature Sensor [part_number=DS18B20]
  Step_down_->_5V = RioRand LM2596
  lx-lifc1-n_charger_with_BMS = 2S-BMS
  VCC1 = Battery
  HDC1080 = gy-213V
  MS5611 = MS5611
  LTR390 = Adafruit LTR390 UV Light Sensor
  RainSensor = Reed switch [package=THT]
  WindSensor = Reed switch [package=THT]  # not connected
  AS5600 = gy-213V

nets:
  3V3: M1.3V3, DS1.VDD
  GND: M1.GND, DS1.GND, Step_down_->_5V.Pin_4
  N1: M1.D4, DS1.DQ
  N2: M1.VIN, Step_down_->_5V.Pin_3
  N3: 7V.A, lx-lifc1-n_charger_with_BMS.pin3#2
  N4: 7V.C, lx-lifc1-n_charger_with_BMS.pin3#3
  N5: Step_down_->_5V.Pin_1, lx-lifc1-n_charger_with_BMS.pin1, VCC1.+
  N6: Step_down_->_5V.Pin_2, lx-lifc1-n_charger_with_BMS.pin2, VCC1.-
  GND_2: HDC1080.GND, MS5611.GND, LTR390.GND, AS5600.GND
  VIN: HDC1080.VIN, MS5611.VIN, LTR390.3.3V, RainSensor.pin_1, AS5600.VIN
  N7: HDC1080.SDA, MS5611.SDA, LTR390.SDA, AS5600.SDA
  N8: HDC1080.SCL, MS5611.SCL, LTR390.SCL, AS5600.SCL

notes:
  I2C
  SCL
  SDA
  VCC 3.3V
  GND
  Solar panel VCC up to 7V
  GND

custom parts:
  DOIT Esp32 DevKit v1 (30 pins long, 11 pins width): The DOIT Esp32 DevKit v1 is one of the development board created by DOIT to evaluate the ESP-WROOM-32 module. It is based on the ESP32 microcontroller that boasts Wifi, Bluetooth, Ethernet and Low Power support all in a single chip. (vanepp) made breadboard work, adjusted pin numbering and labels and reduced size of schematic and cleaned up pcb. This chip is 30pins long (2 x15) and 11 pins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
  2S-BMS: 2S-BMS LIPO battery charger / protection unit. Note pcb does not match the board as it will likely connect with wires, so pcb is 5 pads suitable for .1in header pins.
  Battery: Your standard 2x 18650 battery pack (7.4 Volts)
  gy-213V: GY-213V-HDC1080 Low Power High Precision Humidity Temperature Sensor Module.
  Adafruit LTR390 UV Light Sensor: The LTR390 is one of the few low-cost UV sensors available, and it's a pretty nice one! With both ambient light and UVA sensing with a peak spectral response between 300 and 350nm. You can use it for measuring how much sun you can get before needing to covering up. Unlike the Si1145, this sensor will not give you UV Index readings. However, the Si1145 does UV Index approximations based on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
